# Fritzing sketch BARS1_1.65 (saved by Fritzing 0.9.0b)
circuit board: 3.50331cm x 2.29968cm
breadboards: 1

parts:
  U3_ATtiny84 = SOIC-14 [chip_label=SO16 package=SO]
  J1 = female pin header, 4 pins [form="♀ (female)"]
  J2 = female pin header, 4 pins [form="♀ (female)"]
  U2 = Voltage Regulator LDO [package=sot23-5]
  C3 = Electrolytic Capacitor [capacitance=10µF voltage=16V package="100 mil [THT, electrolytic]"]
  +_- = female pin header, 2 pins [form="♀ (female)"]
  C2 = Electrolytic Capacitor [capacitance=10µF voltage=16V package="100 mil [THT, electrolytic]"]
  Q1 = female pin header, 3 pins [form="♀ (female)"]
  C4 = Capacitor [package=1206]
  U1 = MCP73831 [package=sot23-5]
  C1 = Electrolytic Capacitor [capacitance=10µF voltage=16V package="100 mil [THT, electrolytic]"]
  LED1_gre = LED - 5mm [color="Red (633nm)" package="5 mm [THT]"]
  LED2_red = LED - 5mm [color="Red (633nm)" package="5 mm [THT]"]
  X1 = USB Connectors [package=usb-microb]
  LED3 = LEDs [package=led-1206]
  +_S_Vc_- = Header 4 [package=1x04-smd]
  S1 = SWITCH-DPDT [package=eg2211]
  R1 = Resistor [tolerance=±5% resistance=6.8k package="1206 [SMD]"]
  R3 = Resistor [tolerance=±5% resistance=2.2k package="1206 [SMD]"]
  R2 = Resistor [tolerance=±5% resistance=2.2k package="1206 [SMD]"]
  R10 = Resistor [tolerance=±5% resistance=2.2k package="1206 [SMD]"]
  R11 = Resistor [tolerance=±5% resistance=2.2k package="1206 [SMD]"]
  R12 = Resistor [tolerance=±5% resistance=2.2k package="1206 [SMD]"]
  S2 = Resistor [tolerance=±5% resistance=2.2k part_number=EVQ-P7J01P package="1206 [SMD]"]

nets:
  N1: U3_ATtiny84.1, U2.IN, C2.+, +_S_Vc_-.2, S1.5
  N2: U3_ATtiny84.2, U2.EN
  N3: U3_ATtiny84.3, R10.Pin_1
  N4: U3_ATtiny84.4, J1.pin4
  N5: U3_ATtiny84.5, Q1.pin1, +_S_Vc_-.4, R11.Pin_0
  N6: U3_ATtiny84.6, J2.pin2
  N7: U3_ATtiny84.7, J2.pin4
  N8: U3_ATtiny84.8, J1.pin3
  N9: U3_ATtiny84.9, J2.pin3
  N10: U3_ATtiny84.10, J1.pin2
  N11: U3_ATtiny84.11, Q1.pin2, R11.Pin_1
  N12: U3_ATtiny84.12, +_S_Vc_-.3
  N13: U3_ATtiny84.13, R12.Pin_0, R12.Pin_1
  GND: U3_ATtiny84.14, J2.pin1, U2.GND, C3.-, +_-.pin2, C2.-, Q1.pin3, C4.2, U1.VSS, C1.-, X1.GND, LED3.C, +_S_Vc_-.1, S1.3, S1.6, R1.Pin_0, R3.Pin_0, S2.Pin_0, S2.Pin_1
  N14: J1.pin1, U2.OUT, C3.+
  N15: U2.BP, C4.1
  N16: +_-.pin1, U1.VBAT, S1.4
  N17: U1.STAT, LED1_gre.anode, LED2_red.cathode
  N18: U1.VIN, C1.+, X1.VBUS, R2.Pin_0
  N19: U1.PROG, R1.Pin_1
  N20: LED1_gre.cathode, R3.Pin_1
  N21: LED2_red.anode, R2.Pin_1
  N22: LED3.A, R10.Pin_0
