# Fritzing sketch BARS1_esp8266 (saved by Fritzing 0.9.3b)
circuit board: 5cm x 4.43687cm
breadboards: 1

parts:
  J1 = Nrf24L01+ [package=THT]
  U1 = ESP8266 WiFi Module [part_number=ESP8266]
  R1 = Resistor [tolerance=±5% resistance=10k package="1206 [SMD]"]
  R2 = Resistor [tolerance=±5% resistance=10k package="1206 [SMD]"]
  R3 = Resistor [tolerance=±5% resistance=10k package="1206 [SMD]"]
  R4 = Resistor [tolerance=±5% resistance=10k package="1206 [SMD]"]
  LED1 = LED - 5mm [color="Red (633nm)" package="5 mm [THT]"]
  LED2 = LED - 5mm [color="Red (633nm)" package="5 mm [THT]"]
  R5 = Resistor [tolerance=±5% resistance=1k package="1206 [SMD]"]
  R7 = Resistor [tolerance=±5% resistance=1k package="1206 [SMD]"]
  C5 = Capacitor [part_number="0.1 uF" package=1206]
  C6 = Capacitor [part_number="0.1 uF" package=1206]
  C7 = Capacitor [part_number="0.1 uF" package=1206]
  X2 = USB Connectors [package=usb-mb-h]
  GND-CTS-VCC-TX-RX-DTR = female pin header, 6 pins [form="♀ (female)"]
  J3 = female pin header, 2 pins [form="♀ (female)"]
  S3 = SWITCH-MOMENTARY-2 [package=tactile-switch-1101ne]
  C10 = Capacitor Polarized [package=cpol-radial-100uf-25v]
  C11 = Capacitor Polarized [package=cpol-radial-100uf-25v]
  U2 = Voltage Regulator [package=sot223]

nets:
  GND: J1.GND, U1.GND, LED1.cathode, LED2.cathode, C5.1, C6.2, C7.2, X2.GND, GND-CTS-VCC-TX-RX-DTR.pin1, J3.pin2, S3.2, C10.-, C11.-, U2.ADJ
  N1: J1.CE, U1.GPIO_4
  N2: J1.SCK, U1.GPIO_14
  N3: J1.MISO, U1.GPIO_12
  N4: J1.MOSI, U1.GPIO_13
  N5: J1.CS, U1.GPIO_15
  VCC: J1.VCC, U1.VCC, R1.Pin_0, R2.Pin_0, R3.Pin_0, R4.Pin_0, R7.Pin_0, C6.1, C7.1, GND-CTS-VCC-TX-RX-DTR.pin3, C10.+, U2.OUT
  N6: U1.RXD, GND-CTS-VCC-TX-RX-DTR.pin4
  N7: U1.GPIO_0, R4.Pin_1, J3.pin1
  N8: U1.GPIO_2, R3.Pin_1
  N9: U1.CH_PD, R2.Pin_1
  N10: U1.TXD, GND-CTS-VCC-TX-RX-DTR.pin5
  N11: U1.GPIO_5, R5.Pin_1
  N12: U1.GPIO_16, S3.1
  N13: U1.REST, R1.Pin_1, C5.2
  N14: LED1.anode, R5.Pin_0
  N15: LED2.anode, R7.Pin_1
  N16: X2.VBUS, C11.+, U2.IN

custom parts:
  Nrf24L01+: Modulo radio nRF24L01+
