# Fritzing sketch BARS1_esp8266_1.1 (saved by Fritzing 0.9.3b)
circuit board: 5.5cm x 5.5cm
breadboards: 1

parts:
  J1 = Nrf24L01+ [package=THT]
  R2 = Resistor [tolerance=±5% resistance=10k package="1206 [SMD]"]
  R3 = Resistor [tolerance=±5% resistance=10k package="1206 [SMD]"]
  R4 = Resistor [tolerance=±5% resistance=10k package="1206 [SMD]"]
  LED1_RED = LED - 5mm [color="Red (633nm)" package="5 mm [THT]"]
  LED2_GRE = LED - 5mm [color="Red (633nm)" package="5 mm [THT]"]
  R5 = Resistor [tolerance=±5% resistance=1k package="1206 [SMD]"]
  R7 = Resistor [tolerance=±5% resistance=1k package="1206 [SMD]"]
  C5 = Capacitor [part_number="0.1 uF" package=1206]
  C6 = Capacitor [part_number="0.1 uF" package=1206]
  C7 = Capacitor [part_number="0.1 uF" package=1206]
  X2 = USB Connectors [package=usb-mb-h]
  GND-CTS-VCC-TX-RX-DTR = female pin header, 6 pins [form="♀ (female)"]
  J3 = female pin header, 2 pins [form="♀ (female)"]
  S3 = SWITCH-MOMENTARY-2 [package=tactile-switch-1101ne]
  C10 = Capacitor Polarized [part_number=330uF package=cpol-radial-100uf-25v]
  C11 = Capacitor Polarized [part_number=330uF package=cpol-radial-100uf-25v]
  U2 = Voltage Regulator [package=sot223]
  R8 = Resistor [tolerance=±5% resistance=10k package="1206 [SMD]"]
  R9 = Resistor [tolerance=±5% resistance=10k package="1206 [SMD]"]
  R10 = Resistor [tolerance=±5% resistance=10k package="1206 [SMD]"]
  U3 = ESP8266 WiFi Module [part_number=ESP8266]

nets:
  GND: J1.GND, LED1_RED.cathode, LED2_GRE.cathode, C5.2, C7.2, X2.GND, S3.2, C11.-, U2.ADJ
  N1: J1.CE, U3.GPIO_5
  N2: J1.SCK, U3.GPIO_14
  N3: J1.MISO, U3.GPIO_12
  N4: J1.MOSI, U3.GPIO_13
  N5: J1.CS, R10.Pin_1, U3.GPIO_15
  VCC: J1.VCC, R2.Pin_0, R3.Pin_0, R4.Pin_0, R7.Pin_0, C6.2, C7.1, GND-CTS-VCC-TX-RX-DTR.pin3, C10.+, U2.OUT, R8.Pin_0, R9.Pin_0, U3.VCC
  N6: R2.Pin_1, U3.GPIO_2
  N7: R3.Pin_1, U3.CH_PD
  N8: R4.Pin_1, J3.pin1, U3.GPIO_0
  N9: LED1_RED.anode, R5.Pin_0
  N10: LED2_GRE.anode, R7.Pin_1
  N11: R5.Pin_1, U3.GPIO_4
  N12: C5.1, R8.Pin_1, U3.REST
  N13: C6.1, GND-CTS-VCC-TX-RX-DTR.pin1, J3.pin2, C10.-, R10.Pin_0, U3.GND
  N14: X2.VBUS, C11.+, U2.IN
  N15: GND-CTS-VCC-TX-RX-DTR.pin4, U3.RXD
  N16: GND-CTS-VCC-TX-RX-DTR.pin5, U3.TXD
  N17: S3.1, R9.Pin_1, U3.GPIO_16

custom parts:
  Nrf24L01+: Modulo radio nRF24L01+
  ESP8266 WiFi Module: Generic WiFi Module based on the ESP8266 with onboard PCB antenna and UART communications
