# Fritzing sketch BARS1_1.66 (saved by Fritzing 0.9.3b)
circuit board: 3.5033cm x 2.34882cm
breadboards: 1

parts:
  J1 = female pin header, 4 pins [form="♀ (female)"]
  J2 = female pin header, 4 pins [form="♀ (female)"]
  +_- = female pin header, 2 pins [form="♀ (female)"]
  C5 = Capacitor [package=1206]
  RED = LEDs [package=led-1206]
  GRE = LEDs [package=led-1206]
  WH = LEDs [package=led-1206]
  R13 = Resistor [tolerance=±5% resistance=4.7k package="1206 [SMD]"]
  R12 = Resistor [tolerance=±5% resistance=4.7k package="1206 [SMD]"]
  R11 = Resistor [tolerance=±5% resistance=4.7k package="1206 [SMD]"]
  R10 = Resistor [tolerance=±5% resistance=4.7k package="1206 [SMD]"]
  X1 = USB Connectors [package=usb-microb]
  R1 = Resistor [tolerance=±5% resistance=3.3k package="1206 [SMD]"]
  U1 = MCP73831 [package=sot23-5]
  ATtiny84 = SOIC-14 [chip_label=SO16 package=SO]
  U2 = Voltage Regulator LDO [package=sot23-5]
  C7 = Capacitor [package=1206]
  DS2 = DS18B20 1-Wire Temperature Sensor [part_number=DS18B20]
  C8 = Capacitor [package=1206]
  C1 = Electrolytic Capacitor [capacitance=4.7µF voltage=16V package="100 mil [THT, electrolytic]"]
  C2 = Electrolytic Capacitor [capacitance=10µF voltage=16V package="100 mil [THT, electrolytic]"]
  C3 = Electrolytic Capacitor [capacitance=10µF voltage=16V package="100 mil [THT, electrolytic]"]
  R14 = Resistor [tolerance=±5% resistance=470 package="1206 [SMD]"]

nets:
  N1: J1.pin1, U2.OUT, C8.1, C3.+
  N2: J1.pin2, ATtiny84.10
  N3: J1.pin3, ATtiny84.8
  N4: J1.pin4, ATtiny84.4
  GND: J2.pin1, +_-.pin2, C5.1, WH.C, R12.Pin_0, X1.GND, R1.Pin_0, U1.VSS, ATtiny84.14, U2.GND, C7.2, DS2.GND, C8.2, C1.-, C2.-, C3.-, R14.Pin_1
  N5: J2.pin2, ATtiny84.6
  N6: J2.pin3, ATtiny84.9
  N7: J2.pin4, ATtiny84.7
  N8: +_-.pin1, U1.VBAT
  N9: C5.2, ATtiny84.1, U2.IN, C2.+
  N10: RED.A, R13.Pin_0
  N11: RED.C, GRE.A, U1.STAT
  N12: GRE.C, R12.Pin_1
  N13: WH.A, R10.Pin_0
  N14: R13.Pin_1, X1.VBUS, U1.VIN, C1.+
  N15: R11.Pin_0, ATtiny84.5, DS2.VDD
  N16: R11.Pin_1, ATtiny84.11, DS2.DQ
  N17: R10.Pin_1, ATtiny84.3
  N18: R1.Pin_1, U1.PROG
  N19: ATtiny84.2, U2.EN
  N20: U2.BP, C7.1
